# Fritzing sketch keyboard_numpad (saved by Fritzing 0.9.3b)
circuit board: 1.5cm x 1.5cm
circuit board: 1.5cm x 1.5cm
circuit board: 1.5cm x 1.5cm
circuit board: 1.5cm x 1.5cm
circuit board: 1.5cm x 1.5cm
circuit board: 8cm x 10cm
circuit board: 1.5cm x 1.5cm
circuit board: 1.5cm x 1.5cm
circuit board: 1.5cm x 1.5cm
circuit board: 1.5cm x 1.5cm
circuit board: 1.5cm x 1.5cm
circuit board: 1.5cm x 1.5cm
circuit board: 1.5cm x 1.5cm
circuit board: 1.5cm x 1.5cm
circuit board: 1.5cm x 1.5cm
circuit board: 1.5cm x 1.5cm
circuit board: 1.5cm x 1.5cm
circuit board: 1.5cm x 1.5cm
breadboards: 1

parts:
  KEY = Cherry MX Keyswitch
  KEY_0 = Cherry MX Keyswitch
  KEY_2 = Cherry MX Keyswitch
  KEY_3 = Cherry MX Keyswitch
  KEY_1 = Cherry MX Keyswitch
  KEY_4 = Cherry MX Keyswitch
  KEY_6 = Cherry MX Keyswitch
  KEY_5 = Cherry MX Keyswitch
  KEY_8 = Cherry MX Keyswitch
  KEY_KEY9 = Cherry MX Keyswitch
  KEY_7 = Cherry MX Keyswitch
  KEY_NUMLOCK = Cherry MX Keyswitch
  KEY_* = Cherry MX Keyswitch
  KEY_- = Cherry MX Keyswitch
  KEY_ENTER = Cherry MX Keyswitch
  KEY_+ = Cherry MX Keyswitch
  KEY_-_2 = Cherry MX Keyswitch
  ROW = female pin header, 5 pins [form="♀ (female)"]
  COLUMN = female pin header, 4 pins [form="♀ (female)"]

nets:
  N1: KEY.pin_2, KEY.pin_5, KEY_0.pin_2, KEY_0.pin_5, KEY_ENTER.pin_2, KEY_ENTER.pin_5, ROW.pin5
  N2: KEY.pin_4, KEY_3.pin_4, KEY_6.pin_4, KEY_KEY9.pin_4, KEY_*.pin_4, COLUMN.pin3
  N3: KEY_0.pin_4, KEY_1.pin_4, KEY_4.pin_4, KEY_7.pin_4, KEY_NUMLOCK.pin_4, COLUMN.pin2
  N4: KEY_2.pin_2, KEY_2.pin_5, KEY_3.pin_2, KEY_3.pin_5, KEY_1.pin_2, KEY_1.pin_5, ROW.pin4
  N5: KEY_2.pin_4, KEY_5.pin_4, KEY_8.pin_4, KEY_-.pin_4, COLUMN.pin1
  N6: KEY_4.pin_2, KEY_4.pin_5, KEY_6.pin_2, KEY_6.pin_5, KEY_5.pin_2, KEY_5.pin_5, ROW.pin3
  N7: KEY_8.pin_2, KEY_8.pin_5, KEY_KEY9.pin_2, KEY_KEY9.pin_5, KEY_7.pin_2, KEY_7.pin_5, KEY_+.pin_2, ROW.pin2
  N8: KEY_NUMLOCK.pin_2, KEY_NUMLOCK.pin_5, KEY_*.pin_2, KEY_*.pin_5, KEY_-.pin_2, KEY_-.pin_5, KEY_-_2.pin_2, KEY_-_2.pin_5, ROW.pin1
  N9: KEY_ENTER.pin_4, KEY_+.pin_4, KEY_-_2.pin_4, COLUMN.pin4

notes:
  Num Pad
  v0.1
